// Logisim project cyclic_decoder.circ as structural Verilog: 1 circuit, main circuit ON 16 clock, save encoded sequence
module ON_16_clock__save_encoded_sequence (
  output out_1,
  output DECODED_DATA,
  output out_3,
  output out_4,
  output out_5,
  output out_6,
  output out_7,
  output out_8,
  output out_9,
  output out_10,
  output out_11
);

  wire and_1_out, and_2_out, and_3_out, and_4_out, and_5_out, and_6_out, and_7_out, and_8_out, and_9_out,
       clock_1_out, comparator_1_eq, comparator_2_eq, comparator_3_eq, comparator_4_eq, d_ff_1_q, d_ff_2_q,
       d_ff_3_q, d_ff_4_q, d_ff_5_q, d_ff_6_q, d_ff_7_q, decoder_1_out0, decoder_1_out1, decoder_1_out2,
       decoder_1_out3, decoder_1_out4, decoder_1_out5, decoder_1_out6, decoder_1_out7, decoder_1_out8,
       decoder_1_out9, decoder_1_out10, demultiplexer_1_out0, demultiplexer_1_out1, demultiplexer_1_out2,
       demultiplexer_1_out3, demultiplexer_1_out4, demultiplexer_1_out5, demultiplexer_1_out6,
       demultiplexer_1_out7, demultiplexer_1_out8, demultiplexer_1_out9, demultiplexer_1_out10,
       multiplexer_1_out, not_1_out, not_2_out, not_3_out, not_4_out, not_5_out, not_6_out, not_7_out,
       not_8_out, not_9_out, not_10_out, not_11_out, not_12_out, not_13_out, not_14_out, or_1_out,
       shift_register_1_out, transistor_1_out, transistor_2_out, transistor_3_out, xor_1_out, xor_2_out,
       xor_3_out, xor_4_out;
  wire [3:0] t_ff_1_q, t_ff_5_q;
  wire [14:0] rom_1_data;

  Clock clock_1 (.out(clock_1_out));
  not not_1 (not_1_out, and_2_out);
  and and_1 (and_1_out, clock_1_out, not_1_out);
  D_Flip_Flop d_ff_1 (.clk(and_1_out), .D(1'b1), .Q(d_ff_1_q));  // open: Qn, preset, en, reset
  T_Flip_Flop t_ff_1 (.clk(and_1_out), .T(d_ff_1_q), .Q(t_ff_1_q[0]));  // open: Qn, preset, reset, en
  and and_2 (and_2_out, t_ff_1_q[3], t_ff_1_q[2], t_ff_1_q[1], t_ff_1_q[0]);
  T_Flip_Flop t_ff_2 (.clk(and_1_out), .T(t_ff_1_q[0]), .Q(t_ff_1_q[1]));  // open: Qn, preset, reset, en
  and and_3 (and_3_out, t_ff_1_q[1], t_ff_1_q[0]);
  and and_4 (and_4_out, t_ff_1_q[3], t_ff_1_q[1], t_ff_1_q[0]);
  T_Flip_Flop t_ff_3 (.clk(and_1_out), .T(and_3_out), .Q(t_ff_1_q[2]));  // open: Qn, preset, reset, en
  and and_5 (and_5_out, t_ff_1_q[2], and_3_out);
  T_Flip_Flop t_ff_4 (.clk(and_1_out), .T(and_5_out), .Q(t_ff_1_q[3]));  // open: Qn, preset, reset, en
  Multiplexer #(.select(4)) multiplexer_1 (
    .in0(1'b1), .in1(1'b0), .in2(1'b0), .in3(1'b0), .in4(1'b0), .in5(1'b0), .in6(1'b1), .in7(1'b1),
    .in8(1'b1), .in9(1'b1), .in10(1'b1), .in11(1'b0), .in12(1'b1), .in13(1'b0), .in14(1'b0), .in15(1'b0),
    .out(multiplexer_1_out), .sel(t_ff_1_q), .en(1'b1));
  not not_2 (not_2_out, and_2_out);
  not not_3 (not_3_out, d_ff_2_q);
  D_Flip_Flop #(.trigger("high")) d_ff_2 (.clk(not_3_out), .D(and_4_out), .Q(d_ff_2_q));  // open: Qn, preset, en, reset
  D_Flip_Flop #(.trigger("falling")) d_ff_3 (
    .clk(clock_1_out), .D(and_2_out), .Q(d_ff_3_q));  // open: Qn, preset, en, reset
  Transistor #(.\type ("n"), .gate("br")) transistor_1 (.in(clock_1_out), .out(transistor_1_out), .gate(not_2_out));
  or or_1 (or_1_out, not_3_out, d_ff_3_q);
  D_Flip_Flop #(.trigger("falling")) d_ff_4 (
    .clk(transistor_1_out), .D(xor_1_out), .Q(d_ff_4_q));  // open: Qn, preset, en, reset
  xor xor_1 (xor_1_out, multiplexer_1_out, d_ff_7_q);
  Transistor #(.\type ("n"), .gate("br")) transistor_2 (.in(clock_1_out), .out(transistor_2_out), .gate(or_1_out));
  D_Flip_Flop #(.trigger("falling")) d_ff_5 (
    .clk(transistor_1_out), .D(d_ff_4_q), .Q(d_ff_5_q));  // open: Qn, preset, en, reset
  xor xor_2 (xor_2_out, d_ff_3_q, and_6_out);
  Transistor #(.\type ("n")) transistor_3 (.in(clock_1_out), .out(transistor_3_out), .gate(xor_2_out));
  D_Flip_Flop #(.trigger("falling")) d_ff_6 (
    .clk(transistor_1_out), .D(d_ff_5_q), .Q(d_ff_6_q));  // open: Qn, preset, en, reset
  xor xor_3 (xor_3_out, d_ff_6_q, d_ff_7_q);
  and and_6 (and_6_out, t_ff_5_q[0], t_ff_5_q[1], t_ff_5_q[3]);
  D_Flip_Flop #(.trigger("falling")) d_ff_7 (
    .clk(transistor_1_out), .D(xor_3_out), .Q(d_ff_7_q));  // open: Qn, preset, en, reset
  T_Flip_Flop t_ff_5 (.clk(transistor_3_out), .T(1'b1), .Q(t_ff_5_q[0]));  // open: Qn, preset, reset, en
  Shift_Register #(.length(11)) shift_register_1 (
    .in(multiplexer_1_out), .clk(transistor_2_out), .out(shift_register_1_out));  // open: shift, load, clr, d0, q0, d1, q1, d2, q2, d3, q3, d4, q4, d5, q5, d6, q6, d7, q7, d8, q8, d9, q9, d10, q10
  T_Flip_Flop t_ff_6 (.clk(transistor_3_out), .T(t_ff_5_q[0]), .Q(t_ff_5_q[1]));  // open: Qn, preset, reset, en
  and and_7 (and_7_out, t_ff_5_q[1], t_ff_5_q[0]);
  ROM #(.addrWidth(4), .dataWidth(15)) rom_1 (.addr(t_ff_5_q), .data(rom_1_data));  // open: sel
  T_Flip_Flop t_ff_7 (.clk(transistor_3_out), .T(and_7_out), .Q(t_ff_5_q[2]));  // open: Qn, preset, reset, en
  T_Flip_Flop t_ff_8 (.clk(transistor_3_out), .T(and_8_out), .Q(t_ff_5_q[3]));  // open: Qn, preset, reset, en
  and and_8 (and_8_out, t_ff_5_q[2], and_7_out);
  Comparator #(.width(1)) comparator_1 (.a(d_ff_4_q), .b(rom_1_data[0]), .eq(comparator_1_eq));  // open: gt, lt
  Comparator #(.width(1)) comparator_2 (.a(d_ff_5_q), .b(rom_1_data[4]), .eq(comparator_2_eq));  // open: gt, lt
  Comparator #(.width(1)) comparator_3 (.a(d_ff_6_q), .b(rom_1_data[8]), .eq(comparator_3_eq));  // open: gt, lt
  Comparator #(.width(1)) comparator_4 (.a(d_ff_7_q), .b(rom_1_data[12]), .eq(comparator_4_eq));  // open: gt, lt
  and and_9 (and_9_out, comparator_1_eq, comparator_2_eq, comparator_3_eq, comparator_4_eq);
  xor xor_4 (xor_4_out, shift_register_1_out, and_9_out);
  Demultiplexer #(.select(4)) demultiplexer_1 (
    .out0(demultiplexer_1_out0), .out1(demultiplexer_1_out1), .out2(demultiplexer_1_out2),
    .out3(demultiplexer_1_out3), .out4(demultiplexer_1_out4), .out5(demultiplexer_1_out5),
    .out6(demultiplexer_1_out6), .out7(demultiplexer_1_out7), .out8(demultiplexer_1_out8),
    .out9(demultiplexer_1_out9), .out10(demultiplexer_1_out10), .in(xor_4_out), .sel(t_ff_5_q));  // open: out11, out12, out13, out14, out15, en
  Decoder #(.select(4)) decoder_1 (
    .out0(decoder_1_out0), .out1(decoder_1_out1), .out2(decoder_1_out2), .out3(decoder_1_out3),
    .out4(decoder_1_out4), .out5(decoder_1_out5), .out6(decoder_1_out6), .out7(decoder_1_out7),
    .out8(decoder_1_out8), .out9(decoder_1_out9), .out10(decoder_1_out10), .sel(t_ff_5_q));  // open: out11, out12, out13, out14, out15, en
  S_R_Flip_Flop #(.trigger("high")) s_r_ff_1 (
    .S(demultiplexer_1_out0), .clk(decoder_1_out0), .R(not_4_out), .Q(out_1));  // open: Qn, preset, reset, en
  not not_4 (not_4_out, demultiplexer_1_out0);
  S_R_Flip_Flop #(.trigger("high")) s_r_ff_2 (
    .S(demultiplexer_1_out1), .clk(decoder_1_out1), .R(not_5_out), .Q(DECODED_DATA));  // open: Qn, preset, reset, en
  not not_5 (not_5_out, demultiplexer_1_out1);
  S_R_Flip_Flop #(.trigger("high")) s_r_ff_3 (
    .S(demultiplexer_1_out2), .clk(decoder_1_out2), .R(not_6_out), .Q(out_3));  // open: Qn, preset, reset, en
  not not_6 (not_6_out, demultiplexer_1_out2);
  S_R_Flip_Flop #(.trigger("high")) s_r_ff_4 (
    .S(demultiplexer_1_out3), .clk(decoder_1_out3), .R(not_7_out), .Q(out_4));  // open: Qn, preset, reset, en
  not not_7 (not_7_out, demultiplexer_1_out3);
  S_R_Flip_Flop #(.trigger("high")) s_r_ff_5 (
    .S(demultiplexer_1_out4), .clk(decoder_1_out4), .R(not_8_out), .Q(out_5));  // open: Qn, preset, reset, en
  not not_8 (not_8_out, demultiplexer_1_out4);
  S_R_Flip_Flop #(.trigger("high")) s_r_ff_6 (
    .S(demultiplexer_1_out5), .clk(decoder_1_out5), .R(not_9_out), .Q(out_6));  // open: Qn, preset, reset, en
  not not_9 (not_9_out, demultiplexer_1_out5);
  S_R_Flip_Flop #(.trigger("high")) s_r_ff_7 (
    .S(demultiplexer_1_out6), .clk(decoder_1_out6), .R(not_10_out), .Q(out_7));  // open: Qn, preset, reset, en
  not not_10 (not_10_out, demultiplexer_1_out6);
  S_R_Flip_Flop #(.trigger("high")) s_r_ff_8 (
    .S(demultiplexer_1_out7), .clk(decoder_1_out7), .R(not_11_out), .Q(out_8));  // open: Qn, preset, reset, en
  not not_11 (not_11_out, demultiplexer_1_out7);
  S_R_Flip_Flop #(.trigger("high")) s_r_ff_9 (
    .S(demultiplexer_1_out8), .clk(decoder_1_out8), .R(not_12_out), .Q(out_9));  // open: Qn, preset, reset, en
  not not_12 (not_12_out, demultiplexer_1_out8);
  S_R_Flip_Flop #(.trigger("high")) s_r_ff_10 (
    .S(demultiplexer_1_out9), .clk(decoder_1_out9), .R(not_13_out), .Q(out_10));  // open: Qn, preset, reset, en
  not not_13 (not_13_out, demultiplexer_1_out9);
  S_R_Flip_Flop #(.trigger("high")) s_r_ff_11 (
    .S(demultiplexer_1_out10), .clk(decoder_1_out10), .R(not_14_out), .Q(out_11));  // open: Qn, preset, reset, en
  not not_14 (not_14_out, demultiplexer_1_out10);

  // Notes on the sheet:
  //   ENCODED DATA
  //   16-BIT COUNTER
  //   STOP CURRENT COUNTER
  //   C16
  //   AFTER ALL DATA IS PASSED INTO CHANNEL
  //   ZERO IS GOIN' TO BE PASSED INTO THE CHANNEL
  //   C11
  //   STOP WRITING TO BUFFER
  //   MODULUS 2 DIVIDER
  //   AND SYNDROME COMPUTATION
  //   TEMP BUFFER
  //   HOLDS INFORMATION PART OF MESSAGE
  //   SYNDROM MATRIX
  //   (pre-calculated)
  //   16-BIT COUNTER
  //   contents of rom_1 (hex, n*v repeats v):
  //   1100 110 11 1101 1010 101 1110 111 1111 1011 1001
  //   REGISTER COLUMN SELECTOR
endmodule
