// Logisim project cyclic_encoder.circ as structural Verilog: 1 circuit, main circuit ON 16 clock, save encoded sequence
module ON_16_clock__save_encoded_sequence (
  output out_1,
  output out_2,
  output out_3,
  output out_4,
  output out_5,
  output out_6,
  output out_7,
  output out_8,
  output out_9,
  output out_10,
  output out_11,
  output out_12,
  output out_13,
  output out_14,
  output out_15
);

  wire and_1_out, and_2_out, and_3_out, and_4_out, and_5_out, clock_1_out, d_ff_1_q, d_ff_2_q, d_ff_3_q,
       d_ff_4_q, d_ff_5_q, d_ff_6_q, decoder_1_out0, decoder_1_out1, decoder_1_out2, decoder_1_out3,
       decoder_1_out4, decoder_1_out5, decoder_1_out6, decoder_1_out7, decoder_1_out8, decoder_1_out9,
       decoder_1_out10, decoder_1_out11, decoder_1_out12, decoder_1_out13, decoder_1_out14,
       demultiplexer_1_out0, demultiplexer_1_out1, demultiplexer_1_out2, demultiplexer_1_out3,
       demultiplexer_1_out4, demultiplexer_1_out5, demultiplexer_1_out6, demultiplexer_1_out7,
       demultiplexer_1_out8, demultiplexer_1_out9, demultiplexer_1_out10, demultiplexer_1_out11,
       demultiplexer_1_out12, demultiplexer_1_out13, demultiplexer_1_out14, multiplexer_1_out, not_1_out,
       not_2_out, not_3_out, not_4_out, not_5_out, not_6_out, not_7_out, not_8_out, not_9_out, not_10_out,
       not_11_out, not_12_out, not_13_out, not_14_out, not_15_out, not_16_out, not_17_out, not_18_out,
       not_19_out, transistor_1_out, transistor_2_out, xor_1_out, xor_2_out;
  wire [3:0] t_ff_1_q;

  and and_1 (and_1_out, clock_1_out, not_2_out);
  Clock clock_1 (.out(clock_1_out));
  T_Flip_Flop t_ff_1 (.clk(and_1_out), .T(1'b1), .Q(t_ff_1_q[0]));  // open: Qn, preset, reset, en
  T_Flip_Flop t_ff_2 (.clk(and_1_out), .T(t_ff_1_q[0]), .Q(t_ff_1_q[1]));  // open: Qn, preset, reset, en
  and and_2 (and_2_out, t_ff_1_q[1], t_ff_1_q[0]);
  T_Flip_Flop t_ff_3 (.clk(and_1_out), .T(and_2_out), .Q(t_ff_1_q[2]));  // open: Qn, preset, reset, en
  and and_3 (and_3_out, t_ff_1_q[2], and_2_out);
  T_Flip_Flop t_ff_4 (.clk(and_1_out), .T(and_3_out), .Q(t_ff_1_q[3]));  // open: Qn, preset, reset, en
  not not_1 (not_1_out, d_ff_1_q);
  D_Flip_Flop #(.trigger("high")) d_ff_1 (.clk(not_1_out), .D(and_4_out), .Q(d_ff_1_q));  // open: Qn, preset, en, reset
  and and_4 (and_4_out, t_ff_1_q[0], t_ff_1_q[1], t_ff_1_q[3]);
  and and_5 (and_5_out, t_ff_1_q[0], t_ff_1_q[1], t_ff_1_q[3], t_ff_1_q[2]);
  Multiplexer #(.select(4)) multiplexer_1 (
    .in0(1'b1), .in1(1'b0), .in2(1'b0), .in3(1'b0), .in4(1'b0), .in5(1'b0), .in6(1'b1), .in7(1'b1),
    .in8(1'b1), .in9(1'b1), .in10(1'b1), .out(multiplexer_1_out), .sel(t_ff_1_q));  // open: in11, in12, in13, in14, in15, en
  not not_2 (not_2_out, d_ff_2_q);
  D_Flip_Flop #(.trigger("high")) d_ff_2 (.clk(not_2_out), .D(and_5_out), .Q(d_ff_2_q));  // open: Qn, preset, en, reset
  Transistor #(.\type ("n"), .gate("br")) transistor_1 (
    .in(multiplexer_1_out), .out(transistor_1_out), .gate(not_1_out));
  D_Flip_Flop d_ff_3 (.clk(and_1_out), .D(transistor_2_out), .Q(d_ff_3_q));  // open: Qn, preset, en, reset
  not not_3 (not_3_out, not_1_out);
  D_Flip_Flop d_ff_4 (.clk(and_1_out), .D(d_ff_3_q), .Q(d_ff_4_q));  // open: Qn, preset, en, reset
  D_Flip_Flop d_ff_5 (.clk(and_1_out), .D(d_ff_4_q), .Q(d_ff_5_q));  // open: Qn, preset, en, reset
  xor xor_1 (xor_1_out, d_ff_5_q, transistor_2_out);
  Transistor #(.gate("br")) transistor_2 (.in(xor_2_out), .out(transistor_2_out), .gate(d_ff_1_q));
  Transistor #(.\type ("n"), .gate("br")) transistor_3 (.in(not_4_out), .out(transistor_2_out), .gate(d_ff_1_q));
  not not_4 (not_4_out, d_ff_1_q);
  Transistor #(.\type ("n")) transistor_4 (.in(d_ff_6_q), .out(transistor_1_out), .gate(not_3_out));
  D_Flip_Flop d_ff_6 (.clk(and_1_out), .D(xor_1_out), .Q(d_ff_6_q));  // open: Qn, preset, en, reset
  xor xor_2 (xor_2_out, transistor_1_out, d_ff_6_q);
  Demultiplexer #(.select(4)) demultiplexer_1 (
    .out0(demultiplexer_1_out0), .out1(demultiplexer_1_out1), .out2(demultiplexer_1_out2),
    .out3(demultiplexer_1_out3), .out4(demultiplexer_1_out4), .out5(demultiplexer_1_out5),
    .out6(demultiplexer_1_out6), .out7(demultiplexer_1_out7), .out8(demultiplexer_1_out8),
    .out9(demultiplexer_1_out9), .out10(demultiplexer_1_out10), .out11(demultiplexer_1_out11),
    .out12(demultiplexer_1_out12), .out13(demultiplexer_1_out13), .out14(demultiplexer_1_out14),
    .in(transistor_1_out), .sel(t_ff_1_q));  // open: out15, en
  Decoder #(.select(4)) decoder_1 (
    .out0(decoder_1_out0), .out1(decoder_1_out1), .out2(decoder_1_out2), .out3(decoder_1_out3),
    .out4(decoder_1_out4), .out5(decoder_1_out5), .out6(decoder_1_out6), .out7(decoder_1_out7),
    .out8(decoder_1_out8), .out9(decoder_1_out9), .out10(decoder_1_out10), .out11(decoder_1_out11),
    .out12(decoder_1_out12), .out13(decoder_1_out13), .out14(decoder_1_out14), .sel(t_ff_1_q));  // open: out15, en
  S_R_Flip_Flop #(.trigger("high")) s_r_ff_1 (
    .S(demultiplexer_1_out0), .clk(decoder_1_out0), .R(not_5_out), .Q(out_1));  // open: Qn, preset, reset, en
  not not_5 (not_5_out, demultiplexer_1_out0);
  S_R_Flip_Flop #(.trigger("high")) s_r_ff_2 (
    .S(demultiplexer_1_out1), .clk(decoder_1_out1), .R(not_6_out), .Q(out_2));  // open: Qn, preset, reset, en
  not not_6 (not_6_out, demultiplexer_1_out1);
  S_R_Flip_Flop #(.trigger("high")) s_r_ff_3 (
    .S(demultiplexer_1_out2), .clk(decoder_1_out2), .R(not_7_out), .Q(out_3));  // open: Qn, preset, reset, en
  not not_7 (not_7_out, demultiplexer_1_out2);
  S_R_Flip_Flop #(.trigger("high")) s_r_ff_4 (
    .S(demultiplexer_1_out3), .clk(decoder_1_out3), .R(not_8_out), .Q(out_4));  // open: Qn, preset, reset, en
  not not_8 (not_8_out, demultiplexer_1_out3);
  S_R_Flip_Flop #(.trigger("high")) s_r_ff_5 (
    .S(demultiplexer_1_out4), .clk(decoder_1_out4), .R(not_9_out), .Q(out_5));  // open: Qn, preset, reset, en
  not not_9 (not_9_out, demultiplexer_1_out4);
  S_R_Flip_Flop #(.trigger("high")) s_r_ff_6 (
    .S(demultiplexer_1_out5), .clk(decoder_1_out5), .R(not_10_out), .Q(out_6));  // open: Qn, preset, reset, en
  not not_10 (not_10_out, demultiplexer_1_out5);
  S_R_Flip_Flop #(.trigger("high")) s_r_ff_7 (
    .S(demultiplexer_1_out6), .clk(decoder_1_out6), .R(not_11_out), .Q(out_7));  // open: Qn, preset, reset, en
  not not_11 (not_11_out, demultiplexer_1_out6);
  S_R_Flip_Flop #(.trigger("high")) s_r_ff_8 (
    .S(demultiplexer_1_out7), .clk(decoder_1_out7), .R(not_12_out), .Q(out_8));  // open: Qn, preset, reset, en
  not not_12 (not_12_out, demultiplexer_1_out7);
  S_R_Flip_Flop #(.trigger("high")) s_r_ff_9 (
    .S(demultiplexer_1_out8), .clk(decoder_1_out8), .R(not_13_out), .Q(out_9));  // open: Qn, preset, reset, en
  not not_13 (not_13_out, demultiplexer_1_out8);
  S_R_Flip_Flop #(.trigger("high")) s_r_ff_10 (
    .S(demultiplexer_1_out9), .clk(decoder_1_out9), .R(not_14_out), .Q(out_10));  // open: Qn, preset, reset, en
  not not_14 (not_14_out, demultiplexer_1_out9);
  S_R_Flip_Flop #(.trigger("high")) s_r_ff_11 (
    .S(demultiplexer_1_out10), .clk(decoder_1_out10), .R(not_15_out), .Q(out_11));  // open: Qn, preset, reset, en
  not not_15 (not_15_out, demultiplexer_1_out10);
  S_R_Flip_Flop #(.trigger("high")) s_r_ff_12 (
    .S(demultiplexer_1_out11), .clk(decoder_1_out11), .R(not_16_out), .Q(out_12));  // open: Qn, preset, reset, en
  not not_16 (not_16_out, demultiplexer_1_out11);
  S_R_Flip_Flop #(.trigger("high")) s_r_ff_13 (
    .S(demultiplexer_1_out12), .clk(decoder_1_out12), .R(not_17_out), .Q(out_13));  // open: Qn, preset, reset, en
  not not_17 (not_17_out, demultiplexer_1_out12);
  S_R_Flip_Flop #(.trigger("high")) s_r_ff_14 (
    .S(demultiplexer_1_out13), .clk(decoder_1_out13), .R(not_18_out), .Q(out_14));  // open: Qn, preset, reset, en
  not not_18 (not_18_out, demultiplexer_1_out13);
  S_R_Flip_Flop #(.trigger("high")) s_r_ff_15 (
    .S(demultiplexer_1_out14), .clk(decoder_1_out14), .R(not_19_out), .Q(out_15));  // open: Qn, preset, reset, en
  not not_19 (not_19_out, demultiplexer_1_out14);

  // Notes on the sheet:
  //   Changes state to 1 at 11 o'clock
  //   and saves the state -->
  //   16 bit COUNTER
  //   SAVE THE STATE AND STOP COUNTER AT 16 o'clock
  //   CLOSES at 11 o'clock
  //   x4 + x3 + 1 POLYNOMINAL REGISTER
  //   FEEDBACK DISABLE GATE at 11 o'clock
  //   Opens at 12 o'clock
  //   <---*
  //   *when disabled a 0 is passed to the circuit
  //   Sets certain TRIGGER state to up when it's time
endmodule
