// Logisim project hamming_decoder.circ as structural Verilog: 1 circuit, main circuit main
module main (
  input  \с ,
  input  \с_2 ,
  input  B1,
  input  \с_3 ,
  input  B2,
  input  B3,
  input  B4,
  input  \с_4 ,
  input  B5,
  input  B6,
  input  B7,
  input  B8,
  input  B9,
  input  B10,
  input  B11,
  output B1_2,
  output B2_2,
  output B3_2,
  output B4_2,
  output B5_2,
  output B6_2,
  output B7_2,
  output B8_2,
  output B9_2,
  output B10_2,
  output B11_2
);

  wire and_1_out, and_2_out, and_3_out, and_4_out, and_5_out, and_6_out, and_7_out, and_8_out, and_9_out,
       and_10_out, and_11_out, not_1_out, not_2_out, not_3_out, not_4_out, not_5_out, not_6_out, not_7_out,
       not_8_out, not_9_out, not_10_out, not_11_out, not_12_out, not_13_out, not_14_out, not_15_out,
       not_16_out, not_17_out, not_18_out, not_19_out, not_20_out, not_21_out, not_22_out, not_23_out,
       not_24_out, xor_1_out, xor_2_out, xor_3_out, xor_4_out;

  not not_1 (not_1_out, xor_4_out);
  not not_2 (not_2_out, xor_2_out);
  not not_3 (not_3_out, xor_3_out);
  not not_4 (not_4_out, xor_4_out);
  not not_5 (not_5_out, xor_3_out);
  and and_1 (and_1_out, not_4_out, not_3_out, xor_2_out, not_9_out);
  and and_2 (and_2_out, not_1_out, not_5_out, not_2_out, xor_1_out);
  not not_6 (not_6_out, xor_3_out);
  not not_7 (not_7_out, xor_4_out);
  not not_8 (not_8_out, xor_4_out);
  not not_9 (not_9_out, xor_1_out);
  and and_3 (and_3_out, not_8_out, not_6_out, xor_2_out, xor_1_out);
  not not_10 (not_10_out, xor_4_out);
  not not_11 (not_11_out, xor_2_out);
  not not_12 (not_12_out, xor_2_out);
  not not_13 (not_13_out, xor_1_out);
  and and_4 (and_4_out, not_7_out, xor_3_out, not_12_out, not_13_out);
  and and_5 (and_5_out, not_10_out, xor_3_out, not_11_out, xor_1_out);
  not not_14 (not_14_out, xor_4_out);
  not not_15 (not_15_out, xor_1_out);
  not not_16 (not_16_out, xor_4_out);
  and and_6 (and_6_out, not_16_out, xor_3_out, xor_2_out, not_15_out);
  not not_17 (not_17_out, xor_3_out);
  not not_18 (not_18_out, xor_2_out);
  not not_19 (not_19_out, xor_1_out);
  and and_7 (and_7_out, not_14_out, xor_3_out, xor_2_out, xor_1_out);
  and and_8 (and_8_out, xor_4_out, not_17_out, not_18_out, not_19_out);
  xor xor_1 (xor_1_out, \с , B1, B3, B5, B7, B9, B11);
  xor xor_2 (xor_2_out, B11, B10, B7, \с_2 , B6, B3, B2);
  xor xor_3 (xor_3_out, B7, B6, \с_3 , B5, B4);
  xor xor_4 (xor_4_out, B11, B10, \с_4 , B9, B8);
  not not_20 (not_20_out, xor_3_out);
  not not_21 (not_21_out, xor_3_out);
  not not_22 (not_22_out, xor_2_out);
  and and_9 (and_9_out, xor_4_out, not_20_out, xor_2_out, not_23_out);
  and and_10 (and_10_out, xor_4_out, not_21_out, not_22_out, xor_1_out);
  not not_23 (not_23_out, xor_1_out);
  not not_24 (not_24_out, xor_3_out);
  and and_11 (and_11_out, xor_4_out, not_24_out, xor_2_out, xor_1_out);
  xor xor_5 (B1_2, B1, and_2_out);
  xor xor_6 (B2_2, B2, and_1_out);
  xor xor_7 (B3_2, B3, and_3_out);
  xor xor_8 (B4_2, B4, and_4_out);
  xor xor_9 (B5_2, B5, and_5_out);
  xor xor_10 (B6_2, B6, and_6_out);
  xor xor_11 (B7_2, B7, and_7_out);
  xor xor_12 (B8_2, B8, and_8_out);
  xor xor_13 (B9_2, B9, and_10_out);
  xor xor_14 (B10_2, B10, and_9_out);
  xor xor_15 (B11_2, B11, and_11_out);

  // Notes on the sheet:
  //   С3
  //   С2
  //   С1
  //   С4
endmodule
