// Logisim project hamming_encoder.circ as structural Verilog: 1 circuit, main circuit main
module main (
  input  in_1,
  input  in_2,
  input  in_3,
  input  in_4,
  input  in_5,
  input  in_6,
  input  in_7,
  input  in_8,
  input  in_9,
  input  in_10,
  input  in_11,
  output out_12,
  output out_13,
  output out_14,
  output out_15,
  output out_16,
  output out_17,
  output out_18,
  output out_19,
  output out_20,
  output out_21,
  output out_22,
  output out_23,
  output out_24,
  output out_25,
  output out_26
);

  xor xor_1 (out_12, in_1, in_3, in_5, in_7, in_9, in_11);
  xor xor_2 (out_13, in_2, in_3, in_6, in_7, in_10, in_11);
  xor xor_3 (out_15, in_4, in_5, in_6, in_7);
  xor xor_4 (out_19, in_8, in_9, in_10, in_11);

  assign out_14 = in_1;
  assign out_16 = in_2;
  assign out_17 = in_3;
  assign out_18 = in_4;
  assign out_20 = in_5;
  assign out_21 = in_6;
  assign out_22 = in_7;
  assign out_23 = in_8;
  assign out_24 = in_9;
  assign out_25 = in_10;
  assign out_26 = in_11;
endmodule
