// Logisim project iterative_encoder_decoder.circ as structural Verilog: 1 circuit, main circuit main
module main (
  input  _1,
  input  _2,
  input  _3,
  input  _4,
  input  _5,
  input  _6,
  input  _7,
  input  _8,
  input  _9,
  input  _10,
  input  _11,
  input  _12,
  input  _13,
  input  _14,
  input  _15,
  input  _16,
  input  _17,
  input  _18,
  output _1_2,
  output _2_2,
  output _3_2,
  output _4_2,
  output _5_2,
  output _6_2,
  output _7_2,
  output _8_2,
  output _9_2,
  output _10_2,
  output _11_2,
  output _12_2,
  output _13_2,
  output _14_2,
  output _15_2,
  output _16_2,
  output _17_2,
  output _18_2
);

  wire and_1_out, and_2_out, and_3_out, and_4_out, and_5_out, and_6_out, and_7_out, and_8_out, and_9_out,
       and_10_out, and_11_out, and_12_out, and_13_out, and_14_out, and_15_out, and_16_out, and_17_out,
       and_18_out, not_1_out, xor_1_out, xor_2_out, xor_3_out, xor_4_out, xor_5_out, xor_6_out, xor_7_out,
       xor_8_out, xor_9_out, xor_10_out, xor_29_out, xor_30_out, xor_31_out, xor_32_out, xor_33_out,
       xor_34_out, xor_35_out, xor_36_out, xor_37_out, xor_38_out, xor_39_out, xor_40_out, xor_41_out,
       xor_42_out, xor_43_out, xor_44_out, xor_45_out, xor_46_out;

  ExactlyOne xor_1 (.out(xor_1_out), .in0(_6), .in1(_5), .in2(_4), .in3(_3), .in4(_2), .in5(_1));
  xor xor_2 (xor_2_out, _12, _11, _10, _9, _8, _7);
  xor xor_3 (xor_3_out, _18, _17, _16, _15, _14, _13);
  xor xor_4 (xor_4_out, xor_3_out, xor_2_out, xor_1_out);
  xor xor_5 (xor_5_out, _18, _12, _6);
  xor xor_6 (xor_6_out, _17, _11, _5);
  xor xor_7 (xor_7_out, _16, _10, _4);
  xor xor_8 (xor_8_out, _15, _9, _3);
  xor xor_9 (xor_9_out, _14, _8, _2);
  xor xor_10 (xor_10_out, _13, _7, _1);
  not not_1 (not_1_out, _4);
  xor xor_11 (_1_2, _1, and_18_out);
  xor xor_12 (_2_2, _2, and_16_out);
  xor xor_13 (_3_2, _3, and_17_out);
  xor xor_14 (_4_2, not_1_out, and_15_out);
  xor xor_15 (_5_2, _5, and_14_out);
  xor xor_16 (_6_2, _6, and_13_out);
  xor xor_17 (_7_2, _7, and_10_out);
  xor xor_18 (_8_2, _8, and_11_out);
  xor xor_19 (_9_2, _9, and_12_out);
  xor xor_20 (_10_2, _10, and_8_out);
  xor xor_21 (_11_2, _11, and_9_out);
  xor xor_22 (_12_2, _12, and_7_out);
  xor xor_23 (_13_2, _13, and_1_out);
  xor xor_24 (_14_2, _14, and_2_out);
  xor xor_25 (_15_2, _15, and_3_out);
  xor xor_26 (_16_2, _16, and_4_out);
  xor xor_27 (_17_2, _17, and_5_out);
  xor xor_28 (_18_2, _18, and_6_out);
  and and_1 (and_1_out, xor_46_out, xor_40_out);
  and and_2 (and_2_out, xor_45_out, xor_40_out);
  and and_3 (and_3_out, xor_44_out, xor_40_out);
  and and_4 (and_4_out, xor_43_out, xor_40_out);
  and and_5 (and_5_out, xor_42_out, xor_40_out);
  and and_6 (and_6_out, xor_41_out, xor_40_out);
  and and_7 (and_7_out, xor_38_out, xor_41_out);
  and and_8 (and_8_out, xor_38_out, xor_43_out);
  and and_9 (and_9_out, xor_38_out, xor_42_out);
  xor xor_29 (xor_29_out, _2, _8, _14);
  xor xor_30 (xor_30_out, _1, _7, _13);
  and and_10 (and_10_out, xor_38_out, xor_46_out);
  and and_11 (and_11_out, xor_38_out, xor_45_out);
  and and_12 (and_12_out, xor_38_out, xor_44_out);
  xor xor_31 (xor_31_out, _3, _9, _15);
  xor xor_32 (xor_32_out, _5, _11, _17);
  xor xor_33 (xor_33_out, not_1_out, _10, _16);
  and and_13 (and_13_out, xor_36_out, xor_41_out);
  and and_14 (and_14_out, xor_36_out, xor_42_out);
  and and_15 (and_15_out, xor_36_out, xor_43_out);
  xor xor_34 (xor_34_out, _6, _12, _18);
  and and_16 (and_16_out, xor_36_out, xor_45_out);
  and and_17 (and_17_out, xor_36_out, xor_44_out);
  xor xor_35 (xor_35_out, _1, _2, _3, not_1_out, _5, _6);
  xor xor_36 (xor_36_out, xor_35_out, xor_1_out);
  xor xor_37 (xor_37_out, _7, _8, _9, _10, _11, _12);
  xor xor_38 (xor_38_out, xor_37_out, xor_3_out);
  xor xor_39 (xor_39_out, _13, _14, _15, _16, _17, _18);
  xor xor_40 (xor_40_out, xor_39_out, xor_2_out);
  xor xor_41 (xor_41_out, xor_5_out, xor_34_out);
  xor xor_42 (xor_42_out, xor_6_out, xor_32_out);
  xor xor_43 (xor_43_out, xor_7_out, xor_33_out);
  xor xor_44 (xor_44_out, xor_8_out, xor_31_out);
  xor xor_45 (xor_45_out, xor_9_out, xor_29_out);
  xor xor_46 (xor_46_out, xor_10_out, xor_30_out);
  and and_18 (and_18_out, xor_36_out, xor_46_out);
  // OR_Gate or_1 is placed but not wired
endmodule
